// Logisim project Guess the Number Xtreme.circ as structural Verilog: 20 circuits, main circuit somador4b
module somador4b (
  input  [3:0] in_1,
  input  [3:0] in_2,
  output [4:0] out_3
);

  Adder #(.width(4)) adder_1 (.a(in_1), .b(in_2), .out(out_3[3:0]), .cout(out_3[4]));  // open: cin
endmodule

module comparador5b (
  input  [4:0] in_1,
  input  [4:0] in_2,
  output out_3,
  output out_4,
  output out_5
);

  wire and_1_out, and_2_out, and_3_out, and_4_out, and_5_out, and_6_out, and_7_out, and_8_out,
       comp1b_1_out_3, comp1b_1_out_4, comp1b_1_out_5, comp1b_2_out_3, comp1b_2_out_4, comp1b_2_out_5,
       comp1b_3_out_3, comp1b_3_out_4, comp1b_3_out_5, comp1b_4_out_3, comp1b_4_out_4, comp1b_4_out_5,
       comp1b_5_out_3, comp1b_5_out_4, comp1b_5_out_5;

  comp1b comp1b_1 (.a(in_1[0]), .b(in_2[0]), .out_3(comp1b_1_out_3), .out_4(comp1b_1_out_4), .out_5(comp1b_1_out_5));
  comp1b comp1b_2 (.a(in_1[1]), .b(in_2[1]), .out_3(comp1b_2_out_3), .out_4(comp1b_2_out_4), .out_5(comp1b_2_out_5));
  comp1b comp1b_3 (.a(in_1[4]), .b(in_2[4]), .out_3(comp1b_3_out_3), .out_4(comp1b_3_out_4), .out_5(comp1b_3_out_5));
  comp1b comp1b_4 (.a(in_1[3]), .b(in_2[3]), .out_3(comp1b_4_out_3), .out_4(comp1b_4_out_4), .out_5(comp1b_4_out_5));
  comp1b comp1b_5 (.a(in_1[2]), .b(in_2[2]), .out_3(comp1b_5_out_3), .out_4(comp1b_5_out_4), .out_5(comp1b_5_out_5));
  and and_1 (and_1_out, comp1b_3_out_3, comp1b_4_out_4);
  and and_2 (and_2_out, comp1b_3_out_3, comp1b_4_out_3, comp1b_5_out_4);
  and and_3 (and_3_out, comp1b_3_out_3, comp1b_4_out_3, comp1b_5_out_3, comp1b_2_out_4);
  and and_4 (and_4_out, comp1b_3_out_3, comp1b_4_out_3, comp1b_5_out_3, comp1b_2_out_3, comp1b_1_out_4);
  and and_5 (and_5_out, comp1b_3_out_3, comp1b_4_out_5);
  and and_6 (and_6_out, comp1b_3_out_3, comp1b_4_out_3, comp1b_5_out_5);
  and and_7 (and_7_out, comp1b_3_out_3, comp1b_4_out_3, comp1b_5_out_3, comp1b_2_out_5);
  and and_8 (and_8_out, comp1b_3_out_3, comp1b_4_out_3, comp1b_5_out_3, comp1b_2_out_3, comp1b_1_out_5);
  and and_9 (out_3, comp1b_3_out_3, comp1b_4_out_3, comp1b_5_out_3, comp1b_2_out_3, comp1b_1_out_3);
  or or_1 (out_4, comp1b_3_out_4, and_1_out, and_4_out, and_2_out, and_3_out);
  or or_2 (out_5, comp1b_3_out_5, and_5_out, and_8_out, and_6_out, and_7_out);
endmodule

module comparador4b (
  input  [3:0] in_1,
  input  [3:0] in_2,
  output out_3,
  output out_4,
  output out_5
);

  wire and_1_out, and_2_out, and_3_out, and_4_out, and_5_out, and_6_out, comp1b_1_out_3, comp1b_1_out_4,
       comp1b_1_out_5, comp1b_2_out_3, comp1b_2_out_4, comp1b_2_out_5, comp1b_3_out_3, comp1b_3_out_4,
       comp1b_3_out_5, comp1b_4_out_3, comp1b_4_out_4, comp1b_4_out_5;

  comp1b comp1b_1 (.a(in_1[3]), .b(in_2[3]), .out_3(comp1b_1_out_3), .out_4(comp1b_1_out_4), .out_5(comp1b_1_out_5));
  comp1b comp1b_2 (.a(in_1[2]), .b(in_2[2]), .out_3(comp1b_2_out_3), .out_4(comp1b_2_out_4), .out_5(comp1b_2_out_5));
  comp1b comp1b_3 (.a(in_1[1]), .b(in_2[1]), .out_3(comp1b_3_out_3), .out_4(comp1b_3_out_4), .out_5(comp1b_3_out_5));
  comp1b comp1b_4 (.a(in_1[0]), .b(in_2[0]), .out_3(comp1b_4_out_3), .out_4(comp1b_4_out_4), .out_5(comp1b_4_out_5));
  and and_1 (and_1_out, comp1b_1_out_3, comp1b_2_out_4);
  and and_2 (and_2_out, comp1b_2_out_3, comp1b_1_out_3, comp1b_3_out_4);
  and and_3 (and_3_out, comp1b_1_out_3, comp1b_3_out_3, comp1b_4_out_4, comp1b_2_out_3);
  and and_4 (and_4_out, comp1b_1_out_3, comp1b_2_out_5);
  and and_5 (and_5_out, comp1b_1_out_3, comp1b_2_out_3, comp1b_3_out_5);
  and and_6 (and_6_out, comp1b_1_out_3, comp1b_2_out_3, comp1b_3_out_3, comp1b_4_out_5);
  and and_7 (out_3, comp1b_2_out_3, comp1b_1_out_3, comp1b_3_out_3, comp1b_4_out_3);
  or or_1 (out_4, comp1b_1_out_4, and_1_out, and_2_out, and_3_out);
  or or_2 (out_5, comp1b_1_out_5, and_4_out, and_5_out, and_6_out);
endmodule

module diff5b (
  input  [4:0] in_1,
  input  [4:0] in_2,
  output [4:0] out_3
);

  wire subtrator1b_1_bout, subtrator1b_2_bout, subtrator1b_3_bout, subtrator1b_4_bout;

  subtrator1b subtrator1b_1 (.a(in_1[0]), .b(in_2[0]), .bin(1'b0), .diff(out_3[0]), .bout(subtrator1b_1_bout));
  subtrator1b subtrator1b_2 (
    .a(in_1[1]), .b(in_2[1]), .bin(subtrator1b_1_bout), .diff(out_3[1]), .bout(subtrator1b_2_bout));
  subtrator1b subtrator1b_3 (
    .a(in_1[2]), .b(in_2[2]), .bin(subtrator1b_2_bout), .diff(out_3[2]), .bout(subtrator1b_3_bout));
  subtrator1b subtrator1b_4 (
    .a(in_1[3]), .b(in_2[3]), .bin(subtrator1b_3_bout), .diff(out_3[3]), .bout(subtrator1b_4_bout));
  subtrator1b subtrator1b_5 (.a(in_1[4]), .b(in_2[4]), .bin(subtrator1b_4_bout), .diff(out_3[4]));  // open: bout
endmodule

module subtrator1b (
  input  a,
  input  b,
  input  bin,
  output diff,
  output bout
);

  wire and_1_out, and_2_out, and_3_out, xor_1_out;

  xor xor_1 (xor_1_out, a, b);
  and and_1 (and_1_out, b, bin);
  and and_2 (and_2_out, ~a, bin);  // AND_Gate
  and and_3 (and_3_out, ~a, b);  // AND_Gate
  xor xor_2 (diff, xor_1_out, bin);
  or or_1 (bout, and_1_out, and_2_out, and_3_out);
endmodule

// cores
module cores5b (
  input  [4:0] num,
  output [7:0] vermelho,
  output [7:0] azul
);

  assign vermelho = ~{num, {3{num[4]}}};  // NOT_Gate not_1, 8 bits wide

  assign azul = {num, {3{num[4]}}};
endmodule

module mux1b (
  input  a,
  input  b,
  input  c,
  output x
);

  wire and_1_out, and_2_out, not_1_out;

  not not_1 (not_1_out, a);
  and and_1 (and_1_out, not_1_out, b);
  and and_2 (and_2_out, a, c);
  or or_1 (x, and_1_out, and_2_out);
endmodule

module diffmux5b (
  input  [4:0] x,
  input  [4:0] y,
  output [4:0] out_3
);

  wire comparador5b_1_out_3;
  wire [4:0] mux5b_1_out_4, mux5b_2_out_4;

  comparador5b comparador5b_1 (.in_1(x), .in_2(y), .out_3(comparador5b_1_out_3));  // open: out_4, out_5
  mux5b mux5b_1 (.a(y), .b(x), .chave(comparador5b_1_out_3), .out_4(mux5b_1_out_4));
  diff5b diff5b_1 (.in_1(mux5b_1_out_4), .in_2(mux5b_2_out_4), .out_3(out_3));
  mux5b mux5b_2 (.a(x), .b(y), .chave(comparador5b_1_out_3), .out_4(mux5b_2_out_4));
endmodule

module mux5b (
  input  [4:0] a,
  input  [4:0] b,
  input  chave,
  output [4:0] out_4
);

  mux1b mux1b_1 (.a(chave), .b(a[4]), .c(b[4]), .x(out_4[4]));
  mux1b mux1b_2 (.a(chave), .b(a[3]), .c(b[3]), .x(out_4[3]));
  mux1b mux1b_3 (.a(chave), .b(a[2]), .c(b[2]), .x(out_4[2]));
  mux1b mux1b_4 (.a(chave), .b(a[1]), .c(b[1]), .x(out_4[1]));
  mux1b mux1b_5 (.a(chave), .b(a[0]), .c(b[0]), .x(out_4[0]));
endmodule

module comp1b (
  input  a,
  input  b,
  output out_3,
  output out_4,
  output out_5
);

  wire and_1_out, and_2_out, not_1_out, not_2_out, not_3_out, not_4_out;

  not not_1 (not_1_out, a);
  not not_2 (not_2_out, b);
  not not_3 (not_3_out, b);
  not not_4 (not_4_out, a);
  and and_1 (and_1_out, not_1_out, not_2_out);
  and and_2 (and_2_out, a, b);
  and and_3 (out_4, a, not_3_out);
  and and_4 (out_5, not_4_out, b);
  or or_1 (out_3, and_1_out, and_2_out);
endmodule

module GTN_X (
  input  End_Turno,
  input  Confirmar,
  input  Sortear,
  input  [3:0] x,
  input  [3:0] y,
  output X_CERTO,
  output Y_CERTO,
  output SOMA_CERTA,
  output [7:0] VERMELHO,
  output [7:0] AZUL,
  output [3:0] X_R,
  output [3:0] Y_R
);

  wire comp4b_2_out_3, comp4b_out_3, comp5b_out_3, Soma_Set, X_Set, Y_Set;
  wire [4:0] diffmux_out_3, soma4b_2_out_3, soma4b_out_3;
  wire [7:0] bit_extender_1_out, cores5b_1_azul, cores5b_1_vermelho;

  Random random_1 (.clk(Sortear), .out({Y_R, X_R}));  // open: next, clr
  assign bit_extender_1_out = {{7{Confirmar}}, Confirmar};  // Bit_Extender bit_extender_1
  somador4b soma4b (.in_1(Y_R), .in_2(X_R), .out_3(soma4b_out_3));
  somador4b soma4b_2 (.in_1(x), .in_2(y), .out_3(soma4b_2_out_3));
  S_R_Flip_Flop s_r_ff_1 (.Q(X_CERTO), .preset(X_Set), .reset(End_Turno));  // open: S, clk, R, Qn
  and and_1 (X_Set, Confirmar, comp4b_out_3);
  comparador4b comp4b (.in_1(X_R), .in_2(x), .out_3(comp4b_out_3));  // open: out_4, out_5
  S_R_Flip_Flop s_r_ff_2 (.Q(Y_CERTO), .preset(Y_Set), .reset(End_Turno));  // open: S, clk, R, Qn
  and and_2 (Y_Set, Confirmar, comp4b_2_out_3);
  comparador4b comp4b_2 (.in_1(Y_R), .in_2(y), .out_3(comp4b_2_out_3));  // open: out_4, out_5
  S_R_Flip_Flop s_r_ff_3 (.Q(SOMA_CERTA), .preset(Soma_Set), .reset(End_Turno));  // open: S, clk, R, Qn
  and and_3 (Soma_Set, Confirmar, comp5b_out_3);
  comparador5b comp5b (.in_1(soma4b_out_3), .in_2(soma4b_2_out_3), .out_3(comp5b_out_3));  // open: out_4, out_5
  assign VERMELHO = bit_extender_1_out & cores5b_1_vermelho;  // AND_Gate and_4, 8 bits wide
  cores5b cores5b_1 (.num(diffmux_out_3), .vermelho(cores5b_1_vermelho), .azul(cores5b_1_azul));
  diffmux5b diffmux (.x(soma4b_out_3), .y(soma4b_2_out_3), .out_3(diffmux_out_3));
  assign AZUL = cores5b_1_azul & bit_extender_1_out;  // AND_Gate and_5, 8 bits wide
endmodule

module Estado_de_Jogo (
  input  Iniciar,
  input  Game_Reset,
  output Rodando,
  output End_Config
);

  S_R_Flip_Flop s_r_ff_1 (.Q(Rodando), .Qn(End_Config), .preset(Iniciar), .reset(Game_Reset));  // open: S, clk, R

  // Notes on the sheet:
  //   Circuito de estado de jogo
endmodule

module Controle_de_turnos (
  input  Config,
  input  Iniciar_jogo,
  input  \Avançar_B ,
  input  Tempo_Esgotado_B,
  input  \Avançar_A ,
  input  Tempo_Esgotado_A,
  input  Resetar_jogo,
  output A_jogando,
  output B_jogando
);

  wire and_1_out, or_1_out, or_2_out, or_3_out;

  or or_1 (or_1_out, \Avançar_B , Tempo_Esgotado_B);
  or or_2 (or_2_out, \Avançar_A , Tempo_Esgotado_A);
  or or_3 (or_3_out, or_1_out, or_2_out);
  and and_1 (and_1_out, Config, Iniciar_jogo);
  S_R_Flip_Flop s_r_ff_1 (
    .S(or_1_out), .clk(or_3_out), .R(or_2_out), .Q(A_jogando), .Qn(B_jogando), .preset(and_1_out),
    .reset(Resetar_jogo));

  // Notes on the sheet:
  //   Circuito de Controle de turnos
endmodule

module Palpite_A (
  input  Escolher_A,
  input  \Avançar ,
  input  Confirmar_A,
  input  Reset,
  output [3:0] \Número_X_escolhido ,
  output [3:0] \Número_Y_escolhido ,
  output [3:0] \Número_a_ser_escolhido ,
  output Fim_do_turno,
  output Escolhendo_Y,
  output Escolhendo_X
);

  wire demultiplexer_1_out0, demultiplexer_1_out1, or_1_out;

  Counter #(.width(4), .max('hf)) counter_1 (
    .Q(\Número_a_ser_escolhido ), .clk(Escolher_A), .clr(or_1_out));  // open: load, D, count, carry, preset, down
  or or_1 (or_1_out, \Avançar , Reset);
  Register #(.width(4), .Select("low")) Number_X (
    .D(\Número_a_ser_escolhido ), .Q(\Número_X_escolhido ), .clk(demultiplexer_1_out0), .clr(Reset));  // open: en
  Demultiplexer #(.enable("false")) demultiplexer_1 (
    .out0(demultiplexer_1_out0), .out1(demultiplexer_1_out1), .in(Confirmar_A), .sel(Escolhendo_Y));
  T_Flip_Flop #(.trigger("falling")) t_ff_1 (
    .clk(\Avançar ), .T(1'b1), .Q(Escolhendo_Y), .Qn(Escolhendo_X));  // open: preset, reset
  Register #(.width(4), .Select("low")) Number_Y (
    .D(\Número_a_ser_escolhido ), .Q(\Número_Y_escolhido ), .clk(demultiplexer_1_out1), .clr(Reset));  // open: en
  and and_1 (Fim_do_turno, \Avançar , Escolhendo_Y);

  // Notes on the sheet:
  //   Circuito de Palpites A
endmodule

module Palpite_B (
  input  Escolher_B,
  input  \Avançar ,
  input  Confirmar_B,
  input  Reset,
  output [3:0] \Número_X_escolhido ,
  output [3:0] \Número_Y_escolhido ,
  output [3:0] \Número_a_ser_escolhido ,
  output Fim_do_turno,
  output Escolhendo_Y,
  output Escolhendo_X
);

  wire demultiplexer_1_out0, demultiplexer_1_out1, or_1_out;

  Counter #(.width(4), .max('hf)) counter_1 (
    .Q(\Número_a_ser_escolhido ), .clk(Escolher_B), .clr(or_1_out));  // open: load, D, count, carry, preset, down
  or or_1 (or_1_out, \Avançar , Reset);
  Register #(.width(4), .Select("low")) Number_X (
    .D(\Número_a_ser_escolhido ), .Q(\Número_X_escolhido ), .clk(demultiplexer_1_out0), .clr(Reset));  // open: en
  Demultiplexer #(.enable("false")) demultiplexer_1 (
    .out0(demultiplexer_1_out0), .out1(demultiplexer_1_out1), .in(Confirmar_B), .sel(Escolhendo_Y));
  T_Flip_Flop #(.trigger("falling")) t_ff_1 (
    .clk(\Avançar ), .T(1'b1), .Q(Escolhendo_Y), .Qn(Escolhendo_X));  // open: preset, reset
  Register #(.width(4), .Select("low")) Number_Y (
    .D(\Número_a_ser_escolhido ), .Q(\Número_Y_escolhido ), .clk(demultiplexer_1_out1), .clr(Reset));  // open: en
  and and_1 (Fim_do_turno, \Avançar , Escolhendo_Y);

  // Notes on the sheet:
  //   Circuito de Palpites B
endmodule

module cronometro_A (
  input  A_joganda,
  input  Reset,
  input  Rodando,
  input  Config,
  input  CLK,
  input  m1a,
  input  m0a,
  input  s1a,
  input  s0a,
  output Tempo_Esgotado_A,
  output [3:0] M1A_2,
  output [3:0] M0A_2,
  output [3:0] S1A_2,
  output [3:0] S0A_2
);

  wire A_jogando, and_1_out, and_2_out, and_3_out, and_5_out, and_6_out, and_7_out, and_9_out, Cout0, Cout1,
       Cout2, Cout3, multiplexer_1_out, multiplexer_2_out, multiplexer_3_out, multiplexer_4_out, or_1_out,
       or_2_out, or_3_out, or_4_out, PM, s_r_ff_1_qn;

  and and_1 (and_1_out, Rodando, Cout0, Cout1, Cout2, Cout3);
  S_R_Flip_Flop s_r_ff_1 (
    .Q(Tempo_Esgotado_A), .Qn(s_r_ff_1_qn), .preset(and_1_out), .reset(Reset));  // open: S, clk, R
  and and_2 (and_2_out, Cout1, Cout2, Cout0);
  or or_1 (or_1_out, Config, and_2_out);
  Counter #(.width(4), .max('h5), .trigger("falling")) counter_1 (
    .count(or_1_out), .Q(M1A_2), .carry(Cout3), .clk(multiplexer_1_out), .clr(Reset), .down(and_3_out));  // open: load, D, preset
  and and_3 (and_3_out, A_jogando, Rodando);
  Multiplexer #(.enable("false")) multiplexer_1 (.in0(PM), .in1(m1a), .out(multiplexer_1_out), .sel(Config));
  and and_4 (A_jogando, A_joganda, s_r_ff_1_qn);
  and and_5 (and_5_out, A_jogando, Rodando);
  and and_6 (and_6_out, Cout1, Cout0);
  or or_2 (or_2_out, Config, and_6_out);
  Counter #(.width(4), .max('h9), .trigger("falling")) counter_2 (
    .count(or_2_out), .Q(M0A_2), .carry(Cout2), .clk(multiplexer_2_out), .clr(Reset), .down(and_5_out));  // open: load, D, preset
  Multiplexer #(.enable("false")) multiplexer_2 (.in0(PM), .in1(m0a), .out(multiplexer_2_out), .sel(Config));
  or or_3 (or_3_out, Config, Cout0);
  Counter #(.width(4), .max('h5), .trigger("falling")) counter_3 (
    .count(or_3_out), .Q(S1A_2), .carry(Cout1), .clk(multiplexer_3_out), .clr(Reset), .down(and_7_out));  // open: load, D, preset
  and and_7 (and_7_out, A_jogando, Rodando);
  Multiplexer #(.enable("false")) multiplexer_3 (.in0(PM), .in1(s1a), .out(multiplexer_3_out), .sel(Config));
  and and_8 (PM, CLK, A_jogando);
  or or_4 (or_4_out, Config, A_jogando);
  Counter #(.width(4), .max('h9), .trigger("falling")) counter_4 (
    .count(or_4_out), .Q(S0A_2), .carry(Cout0), .clk(multiplexer_4_out), .clr(Reset), .down(and_9_out));  // open: load, D, preset
  and and_9 (and_9_out, A_jogando, Rodando);
  Multiplexer #(.enable("false")) multiplexer_4 (.in0(PM), .in1(s0a), .out(multiplexer_4_out), .sel(Config));

  // Other names for the same wires on the sheet: v0[3:0] = S0A_2; v1[3:0] = S1A_2; v2[3:0] = M0A_2; v3[3:0] = M1A_2

  // Notes on the sheet:
  //   Cronômetro A
endmodule

module cronometro_B (
  input  B_joganda,
  input  Reset,
  input  Rodando,
  input  Config,
  input  CLK,
  input  m1b,
  input  m0b,
  input  s1b,
  input  s0b,
  output Tempo_Esgotado_B,
  output [3:0] M1B_2,
  output [3:0] M0B_2,
  output [3:0] S1B_2,
  output [3:0] S0B_2
);

  wire and_1_out, and_2_out, and_3_out, and_5_out, and_6_out, and_7_out, and_8_out, B_jogando, Cout0, Cout1,
       Cout2, Cout3, multiplexer_1_out, multiplexer_2_out, multiplexer_3_out, multiplexer_4_out, or_1_out,
       or_2_out, or_3_out, or_4_out, PM, s_r_ff_1_qn;

  and and_1 (and_1_out, Rodando, Cout0, Cout1, Cout2, Cout3);
  and and_2 (and_2_out, Cout1, Cout2, Cout0);
  or or_1 (or_1_out, Config, and_2_out);
  Counter #(.width(4), .max('h5), .trigger("falling")) counter_1 (
    .count(or_1_out), .Q(M1B_2), .carry(Cout3), .clk(multiplexer_1_out), .clr(Reset), .down(and_3_out));  // open: load, D, preset
  and and_3 (and_3_out, B_jogando, Rodando);
  Multiplexer #(.enable("false")) multiplexer_1 (.in0(PM), .in1(m1b), .out(multiplexer_1_out), .sel(Config));
  S_R_Flip_Flop s_r_ff_1 (
    .Q(Tempo_Esgotado_B), .Qn(s_r_ff_1_qn), .preset(and_1_out), .reset(Reset));  // open: S, clk, R
  and and_4 (B_jogando, B_joganda, s_r_ff_1_qn);
  and and_5 (and_5_out, B_jogando, Rodando);
  and and_6 (and_6_out, Cout1, Cout0);
  or or_2 (or_2_out, Config, and_6_out);
  Counter #(.width(4), .max('h9), .trigger("falling")) counter_2 (
    .count(or_2_out), .Q(M0B_2), .carry(Cout2), .clk(multiplexer_2_out), .clr(Reset), .down(and_5_out));  // open: load, D, preset
  Multiplexer #(.enable("false")) multiplexer_2 (.in0(PM), .in1(m0b), .out(multiplexer_2_out), .sel(Config));
  or or_3 (or_3_out, Config, Cout0);
  Counter #(.width(4), .max('h5), .trigger("falling")) counter_3 (
    .count(or_3_out), .Q(S1B_2), .carry(Cout1), .clk(multiplexer_3_out), .clr(Reset), .down(and_7_out));  // open: load, D, preset
  and and_7 (and_7_out, B_jogando, Rodando);
  Multiplexer #(.enable("false")) multiplexer_3 (.in0(PM), .in1(s1b), .out(multiplexer_3_out), .sel(Config));
  or or_4 (or_4_out, Config, B_jogando);
  Counter #(.width(4), .max('h9), .trigger("falling")) counter_4 (
    .count(or_4_out), .Q(S0B_2), .carry(Cout0), .clk(multiplexer_4_out), .clr(Reset), .down(and_8_out));  // open: load, D, preset
  and and_8 (and_8_out, B_jogando, Rodando);
  Multiplexer #(.enable("false")) multiplexer_4 (.in0(PM), .in1(s0b), .out(multiplexer_4_out), .sel(Config));
  and and_9 (PM, CLK, B_jogando);

  // Notes on the sheet:
  //   Cronômetro B
endmodule

module Placar (
  input  Confirmar_A,
  input  A_jogando,
  input  X_certo,
  input  Y_certo,
  input  Soma_certa,
  input  B_jogando,
  input  Confirmar_B,
  input  Reset,
  output Acerto_A,
  output [3:0] Ponto_A,
  output [3:0] Ponto_B,
  output Acerto_B
);

  and and_1 (Acerto_A, Confirmar_A, A_jogando, Soma_certa, X_certo, Y_certo);
  and and_2 (Acerto_B, Y_certo, X_certo, Soma_certa, B_jogando, Confirmar_B);
  Counter #(.width(4), .max('hf)) counter_1 (
    .Q(Ponto_A), .clk(Acerto_A), .clr(Reset));  // open: load, D, count, carry, preset, down
  Counter #(.width(4), .max('hf)) counter_2 (
    .Q(Ponto_B), .clk(Acerto_B), .clr(Reset));  // open: load, D, count, carry, preset, down

  // Other names for the same wires on the sheet: sc = Soma_certa

  // Notes on the sheet:
  //   Placar
endmodule

module \Teste_Cronômetro_AB  (
);

  wire A_jogando, A_Venceu, Acerto_A, Acerto_B, \Avançar_A , \Avançar_B , B_jogando, B_Venceu, clk, Config,
       Confirmar_A, Confirmar_B, End_turno_A, End_turno_B, Escolhendo_X, Escolhendo_X_A, Escolhendo_X_B,
       Escolhendo_Y, Escolhendo_Y_A, Escolhendo_Y_B, Escolher_A, Escolher_B, Iniciar, m0a_t, m0b_t, m1a_t,
       m1b_t, multiplexer_5_out, or_1_out, or_2_out, Reset, Rodando, s0a_t, s0b_t, s1a_t, s1b_t, Soma_certa,
       Sortear, Tempo_Esgotado_A, Tempo_Esgotado_B, Turno_Led, X_certo, Y_certo;
  wire [3:0] gtn_x_1_x_r, gtn_x_1_y_r, M0A, M0B, M1A, M1B, multiplexer_6_out, multiplexer_8_out, Placar_A,
       Placar_B, S0A, S0B, S1A, S1B, V_A, V_B, X_Escolhido, X_Escolhido_A, X_Escolhido_B, Y_Escolhido,
       Y_Escolhido_A, Y_Escolhido_B;
  wire [7:0] B, R;

  Controle_de_turnos controle_de_turnos_1 (
    .\Avançar_B (End_turno_B), .\Avançar_A (End_turno_A), .A_jogando(A_jogando), .B_jogando(B_jogando),
    .Iniciar_jogo(Iniciar), .Resetar_jogo(Reset), .Tempo_Esgotado_A(Tempo_Esgotado_A),
    .Tempo_Esgotado_B(Tempo_Esgotado_B), .Config(Config));
  Clock clock_1 (.out(clk));
  Hex_Digit_Display hex_digit_display_1 (.value(M1A));  // open: dp
  Button button_1 (.out(m1a_t));
  Button button_2 (.out(Escolher_A));
  Hex_Digit_Display hex_digit_display_2 (.value(Placar_A));  // open: dp
  Hex_Digit_Display hex_digit_display_3 (.value(M0A));  // open: dp
  Button button_3 (.out(m0a_t));
  Hex_Digit_Display hex_digit_display_4 (.value(V_A));  // open: dp
  Button button_4 (.out(Confirmar_A));
  LED led_1 (.in(A_jogando));
  Placar placar_1 (
    .Confirmar_A(Confirmar_A), .A_jogando(A_jogando), .X_certo(X_certo), .Y_certo(Y_certo),
    .B_jogando(B_jogando), .Confirmar_B(Confirmar_B), .Reset(Reset), .Ponto_A(Placar_A), .Ponto_B(Placar_B),
    .Acerto_A(Acerto_A), .Acerto_B(Acerto_B), .Soma_certa(Soma_certa));
  Hex_Digit_Display hex_digit_display_5 (.value(S0A));  // open: dp
  Hex_Digit_Display hex_digit_display_6 (.value(S1A));  // open: dp
  Button button_5 (.out(s0a_t));
  Button button_6 (.out(s1a_t));
  Estado_de_Jogo estado_de_jogo_1 (.Iniciar(Iniciar), .Game_Reset(Reset), .Rodando(Rodando), .End_Config(Config));
  Button button_7 (.out(\Avançar_A ));
  cronometro_A cronometro_a_1 (
    .A_joganda(A_jogando), .Reset(Reset), .Rodando(Rodando), .Config(Config), .CLK(clk), .M1A_2(M1A),
    .M0A_2(M0A), .S1A_2(S1A), .S0A_2(S0A), .m1a(m1a_t), .m0a(m0a_t), .s1a(s1a_t), .s0a(s0a_t),
    .Tempo_Esgotado_A(Tempo_Esgotado_A));
  Palpite_A palpite_a_1 (
    .\Número_a_ser_escolhido (V_A), .\Número_X_escolhido (X_Escolhido_A),
    .\Número_Y_escolhido (Y_Escolhido_A), .Escolher_A(Escolher_A), .Confirmar_A(Confirmar_A),
    .\Avançar (\Avançar_A ), .Escolhendo_Y(Escolhendo_Y_A), .Escolhendo_X(Escolhendo_X_A),
    .Fim_do_turno(End_turno_A), .Reset(Reset));
  Multiplexer #(.width(4), .enable("false")) multiplexer_1 (
    .in0(X_Escolhido_B), .in1(X_Escolhido_A), .out(X_Escolhido), .sel(A_jogando));
  LED led_2 (.in(X_certo));
  LED led_3 (.in(A_Venceu));
  LED led_4 (.in(Soma_certa));
  Hex_Digit_Display hex_digit_display_7 (.value(X_Escolhido));  // open: dp
  LED led_5 (.in(Escolhendo_X));
  Button button_8 (.out(Iniciar));
  LED led_6 (.in(B_Venceu));
  Button button_9 (.out(Reset));
  Multiplexer #(.width(4), .enable("false")) multiplexer_2 (
    .in0(Y_Escolhido_B), .in1(Y_Escolhido_A), .out(Y_Escolhido), .sel(A_jogando));
  // RGBLed #(.multibit("true")) rgbled_1: pin names not known; wires that end beside it: R, B
  Hex_Digit_Display hex_digit_display_8 (.value(Y_Escolhido));  // open: dp
  LED led_7 (.in(Escolhendo_Y));
  Button button_10 (.out(Sortear));
  LED led_8 (.in(Y_certo));
  cronometro_B cronometro_b_1 (
    .B_joganda(B_jogando), .Reset(Reset), .Rodando(Rodando), .Config(Config), .CLK(clk), .M1B_2(M1B),
    .M0B_2(M0B), .S1B_2(S1B), .S0B_2(S0B), .m1b(m1b_t), .m0b(m0b_t), .s1b(s1b_t), .s0b(s0b_t),
    .Tempo_Esgotado_B(Tempo_Esgotado_B));
  Multiplexer #(.enable("false")) multiplexer_3 (
    .in0(Escolhendo_X_B), .in1(Escolhendo_X_A), .out(Escolhendo_X), .sel(A_jogando));
  Palpite_B palpite_b_1 (
    .Fim_do_turno(End_turno_B), .Escolhendo_Y(Escolhendo_Y_B), .Escolhendo_X(Escolhendo_X_B),
    .\Número_a_ser_escolhido (V_B), .\Número_X_escolhido (X_Escolhido_B),
    .\Número_Y_escolhido (Y_Escolhido_B), .Escolher_B(Escolher_B), .Confirmar_B(Confirmar_B),
    .\Avançar (\Avançar_B ), .Reset(Reset));
  Hex_Digit_Display hex_digit_display_9 (.value(M1B));  // open: dp
  Hex_Digit_Display hex_digit_display_10 (.value(M0B));  // open: dp
  Button button_11 (.out(m0b_t));
  Button button_12 (.out(m1b_t));
  Button button_13 (.out(Escolher_B));
  Hex_Digit_Display hex_digit_display_11 (.value(Placar_B));  // open: dp
  Hex_Digit_Display hex_digit_display_12 (.value(S1B));  // open: dp
  Button button_14 (.out(s1b_t));
  Hex_Digit_Display hex_digit_display_13 (.value(V_B));  // open: dp
  Button button_15 (.out(Confirmar_B));
  LED led_9 (.in(B_jogando));
  Hex_Digit_Display hex_digit_display_14 (.value(S0B));  // open: dp
  Button button_16 (.out(s0b_t));
  Button button_17 (.out(\Avançar_B ));
  Multiplexer #(.enable("false")) multiplexer_4 (
    .in0(Escolhendo_Y_B), .in1(Escolhendo_Y_A), .out(Escolhendo_Y), .sel(A_jogando));
  Multiplexer #(.enable("false")) multiplexer_5 (
    .in0(Confirmar_B), .in1(Confirmar_A), .out(multiplexer_5_out), .sel(A_jogando));
  or or_1 (or_1_out, Acerto_A, Acerto_B, Iniciar, Sortear);
  Multiplexer #(.width(4), .enable("false")) multiplexer_6 (
    .in0(X_Escolhido_B), .in1(X_Escolhido), .out(multiplexer_6_out), .sel(A_jogando));
  Multiplexer #(.enable("false")) multiplexer_7 (
    .in0(\Avançar_B ), .in1(\Avançar_A ), .out(Turno_Led), .sel(A_jogando));
  Vitoria vitoria_1 (
    .Pontos_A(Placar_A), .Pontos_B(Placar_B), .Pontos_A_2(Placar_A), .Pontos_B_2(Placar_B),
    .Tempo_esgotado_A(Tempo_Esgotado_A), .Tempo_esgotado_B(Tempo_Esgotado_B), .A_Venceu(A_Venceu),
    .B_Venceu(B_Venceu));
  or or_2 (or_2_out, Reset, Turno_Led);
  GTN_X gtn_x_1 (
    .Confirmar(multiplexer_5_out), .Sortear(or_1_out), .x(multiplexer_6_out), .y(multiplexer_8_out),
    .X_CERTO(X_certo), .SOMA_CERTA(Soma_certa), .VERMELHO(R), .AZUL(B), .X_R(gtn_x_1_x_r), .Y_R(gtn_x_1_y_r),
    .Y_CERTO(Y_certo), .End_Turno(or_2_out));
  Multiplexer #(.width(4), .enable("false")) multiplexer_8 (
    .in0(Y_Escolhido_B), .in1(Y_Escolhido_A), .out(multiplexer_8_out), .sel(A_jogando));
  Hex_Digit_Display hex_digit_display_15 (.value(gtn_x_1_x_r));  // open: dp
  Hex_Digit_Display hex_digit_display_16 (.value(gtn_x_1_y_r));  // open: dp

  // Notes on the sheet:
  //   Controle de turnos
  //   :
  //   Estado de jogo
  //   Teste
  //   :
endmodule

module Vitoria (
  input  [3:0] Pontos_A,
  input  [3:0] Pontos_B,
  input  [3:0] Pontos_A_2,
  input  [3:0] Pontos_B_2,
  input  Tempo_esgotado_A,
  input  Tempo_esgotado_B,
  output A_Venceu,
  output B_Venceu
);

  wire A15, A_Ganhou_Por_Tempo, B15, B_Ganhou_Por_Tempo, comparator_1_gt, comparator_1_lt, Sem_Tempo;

  and and_1 (A15, Pontos_A[0], Pontos_A[1], Pontos_A[2], Pontos_A[3]);
  and and_2 (B15, Pontos_B[0], Pontos_B[1], Pontos_B[2], Pontos_B[3]);
  Comparator #(.width(4)) comparator_1 (
    .a(Pontos_A_2), .b(Pontos_B_2), .gt(comparator_1_gt), .lt(comparator_1_lt));  // open: eq
  and and_3 (Sem_Tempo, Tempo_esgotado_A, Tempo_esgotado_B);
  and and_4 (A_Ganhou_Por_Tempo, comparator_1_gt, Sem_Tempo);
  and and_5 (B_Ganhou_Por_Tempo, Sem_Tempo, comparator_1_lt);
  or or_1 (A_Venceu, A15, A_Ganhou_Por_Tempo);
  or or_2 (B_Venceu, B15, B_Ganhou_Por_Tempo);
endmodule
